# Fritzing sketch Schema (saved by Fritzing 0.9.3b)
breadboards: 1

parts:
  Part3 = Arduino Nano (Rev3.0) (ICSP)
  Part4 = Bluetooth HC-05 Macho
  ZS-042_RTC1 = ZS-042 RTC Module
  DHT1 = DHT11 Humitidy and Temperature Sensor
  U2 = Mini-USB _B_ connector with 5th pin broken out. [package=usb-micro_b]
  R1 = Resistor [tolerance=±5% resistance=10k package=THT]
  R2 = Resistor [tolerance=±5% resistance=1k package=THT]
  R3 = Resistor [tolerance=±5% resistance=2.2k package=THT]
  Part7 = ws2812b [package="smd 2812b"]
  Part8 = ws2812b [package="smd 2812b"]
  Part9 = ws2812b [package="smd 2812b"]
  R4 = Resistor [tolerance=±5% resistance=330 package="2010 [SMD]"]

nets:
  GND: Part3.GND, Part4.GND, ZS-042_RTC1.GND, DHT1.GND, U2.D-, R3.Pin_1, Part7.VSS, Part8.VSS
  N1: Part3.D6, R4.Pin_1
  N2: Part3.D8, Part4.TXD
  N3: Part3.D9, R2.Pin_0
  N4: Part3.D12/MISO, DHT1.DATA, R1.Pin_0
  VDD: Part3.VIN, Part4.VCC, ZS-042_RTC1.VCC, DHT1.VDD, U2.VBUS, R1.Pin_1, Part7.VDD, Part8.VDD, Part9.VDD
  N5: Part3.A5, ZS-042_RTC1.SCL
  N6: Part3.A4, ZS-042_RTC1.SDA
  N7: Part4.RXD, R2.Pin_1, R3.Pin_0
  N8: Part7.DIN, Part8.DOUT
  N9: Part8.DIN, Part9.DOUT
  N10: Part9.DIN, R4.Pin_0

notes:
  WS2812B LED strip (etc.)

custom parts:
  DHT11 Humitidy and Temperature Sensor: DHT11 Humidity and Temperature Sensor
